// Logisim project cpu.circ as structural Verilog: 3 circuits, main circuit main
module main (
  input  [31:0] INSTRUCTION,
  input  CLOCK,
  output [31:0] FETCH_ADDRESS,
  output [31:0] ra_Value,
  output [31:0] sp_Value,
  output [31:0] t0_Value,
  output [31:0] t1_Value,
  output [31:0] t2_Value,
  output [31:0] s0_Value,
  output [31:0] s1_Value,
  output [31:0] a0_Value
);

  wire MEM_p1, MEM_p2, MEM_p4, MEM_p7, MEM_p9, MEM_p11, RegWEn;
  wire [31:0] ALU, multiplexer_1_out, PC_4, RS1, RS2, WB;

  Multiplexer #(.width(32)) multiplexer_1 (.in0(ALU), .in1(PC_4), .out(multiplexer_1_out));  // open: sel, en
  Register #(.width(32)) PC (.D(multiplexer_1_out), .Q(FETCH_ADDRESS), .clk(CLOCK));  // open: en, clr
  Adder #(.width(32)) adder_1 (.a(FETCH_ADDRESS), .b(32'h4), .out(PC_4));  // open: cin, cout
  regfile_main main_1 (
    .Read_Register_1__rs1(INSTRUCTION[19:15]), .Read_Register_2__rs2(INSTRUCTION[24:20]),
    .Write_Register__rd(INSTRUCTION[11:7]), .Write_Data(WB), .Write_Enable(RegWEn), .Clock(CLOCK),
    .Read_Data_1(RS1), .Read_Data_2(RS2), .ra_Value(ra_Value), .sp_Value(sp_Value), .t0_Value(t0_Value),
    .t1_Value(t1_Value), .t2_Value(t2_Value), .s0_Value(s0_Value), .s1_Value(s1_Value), .a0_Value(a0_Value));
  alu_main main_2 (.Switch(4'b0100), .X(32'h4), .Result(ALU), .Y(32'h4));  // open: Equal
  // mem_main MEM: pin names not known; wires that end beside it: MEM_p1, MEM_p2, MEM_p2, MEM_p4, CLOCK, MEM_p4, MEM_p7, MEM_p7, MEM_p9, MEM_p9, MEM_p11

  // Other names for the same wires on the sheet: a0[31:0] = a0_Value; clk = CLOCK; fetch_addr[31:0] = FETCH_ADDRESS;
  //   ra[31:0] = ra_Value; s0[31:0] = s0_Value; s1[31:0] = s1_Value; sp[31:0] = sp_Value; t0[31:0] = t0_Value;
  //   t1[31:0] = t1_Value; t2[31:0] = t2_Value; CONTROL[31:0] = INSTRUCTION; to_IMMGEN[31:0] = INSTRUCTION

  // Notes on the sheet:
  //   Output
  //   These are outputs/inputs from run.circ
  //   Inputs
endmodule

module Control (
  input  [31:0] in_1
);
endmodule

module opcode_ID (
  input  [6:0] in_1
);

  Comparator #(.width(7)) comparator_1 (.a({7{1'b0}}), .b(in_1));  // open: gt, eq, lt
  Comparator #(.width(7)) comparator_2 (.a(7'b0110011), .b(in_1));  // open: gt, eq, lt
  Comparator #(.width(7)) comparator_3 (.a(7'b0000011), .b(in_1));  // open: gt, eq, lt
  Comparator #(.width(7)) comparator_4 (.a(7'b0010011), .b(in_1));  // open: gt, eq, lt
  Comparator #(.width(7)) comparator_5 (.a(7'b0100011), .b(in_1));  // open: gt, eq, lt
  Comparator #(.width(7)) comparator_6 (.a(7'b1100011), .b(in_1));  // open: gt, eq, lt
  Comparator #(.width(7)) comparator_7 (.a(7'b0110111), .b(in_1));  // open: gt, eq, lt
  Comparator #(.width(7)) comparator_8 (.a(7'b1101111), .b(in_1));  // open: gt, eq, lt
  Comparator #(.width(7)) comparator_9 (.a(7'b1100111), .b(in_1));  // open: gt, eq, lt

  // Other names for the same wires on the sheet: opcode[6:0] = in_1
endmodule
